// Logisim project FLIP8_Simulation.circ as structural Verilog: 5 circuits, main circuit main
module main (
  input  [7:0] in_1,
  input  in_2,
  input  in_3
);

  wire button_1_out, clock_1_out, controlled_buffer_10_out, decoder_1_out1, decoder_1_out2, decoder_1_out3,
       decoder_1_out4, decoder_1_out5, decoder_1_out6, decoder_1_out7, decoder_2_out1, decoder_2_out2,
       decoder_2_out3, decoder_2_out4, decoder_2_out5, decoder_2_out6, decoder_2_out7, decoder_3_out0,
       decoder_3_out1, decoder_3_out2, decoder_3_out3, n7_segment_display_1_p1, n7_segment_display_2_p1,
       n7_segment_display_3_p1, n7_segment_display_4_p1, n7_segment_display_5_p1, n7_segment_display_6_p1,
       n7_segment_display_7_p1, n7_segment_display_8_p1, n7_segment_display_9_p1, not_1_out, not_2_out,
       or_1_out, or_2_out, singlenumbercond_1_result;
  wire [0:0] rom_1_data_3;
  wire [1:0] rom_1_data_4;
  wire [2:0] rom_1_data_2;
  wire [4:3] rom_1_data;
  wire [7:0] alu_1_aluoutput, controlled_buffer_1_out, controlled_buffer_2_out, controlled_buffer_8_out,
       counter_1_q, dipswitch_1_sw8, register_1_q, register_2_q, register_3_q, register_4_q, register_5_q;

  Button button_1 (.out(button_1_out));
  Clock clock_1 (.out(clock_1_out));
  Counter counter_1 (
    .clr(button_1_out), .load(controlled_buffer_10_out), .clk(clock_1_out), .D(controlled_buffer_2_out),
    .Q(counter_1_q));  // open: up, count, carry
  Register register_1 (.D(in_1), .en(in_2), .clk(in_3), .Q(register_1_q));  // open: clr
  // _7_Segment_Display 7_segment_display_1: pin names not known; wires that end beside it: n7_segment_display_1_p1, n7_segment_display_1_p1
  // BCD_to_7_Segment_decoder bcd_to_7_segment_decoder_1: pin names not known; wires that end beside it: in_1
  // Binary_to_BCD_converter #(.binvalue(8)) binary_to_bcd_converter_1: pin names not known; wires that end beside it: register_1_q
  ROM rom_1 (.addr(counter_1_q), .data({rom_1_data_4, rom_1_data_3[0], rom_1_data, rom_1_data_2}));
  // _7_Segment_Display 7_segment_display_2: pin names not known; wires that end beside it: n7_segment_display_2_p1, n7_segment_display_2_p1
  // BCD_to_7_Segment_decoder bcd_to_7_segment_decoder_2: pin names not known
  // _7_Segment_Display 7_segment_display_3: pin names not known; wires that end beside it: n7_segment_display_3_p1, n7_segment_display_3_p1
  // BCD_to_7_Segment_decoder bcd_to_7_segment_decoder_3: pin names not known
  DipSwitch dipswitch_1 (
    .sw1(dipswitch_1_sw8[7]), .sw2(dipswitch_1_sw8[6]), .sw3(dipswitch_1_sw8[5]), .sw4(dipswitch_1_sw8[4]),
    .sw5(dipswitch_1_sw8[3]), .sw6(dipswitch_1_sw8[2]), .sw7(dipswitch_1_sw8[1]), .sw8(dipswitch_1_sw8[0]));
  // _7_Segment_Display 7_segment_display_4: pin names not known; wires that end beside it: n7_segment_display_4_p1, n7_segment_display_4_p1
  // _7_Segment_Display 7_segment_display_5: pin names not known; wires that end beside it: n7_segment_display_5_p1, n7_segment_display_5_p1
  // BCD_to_7_Segment_decoder bcd_to_7_segment_decoder_4: pin names not known
  // BCD_to_7_Segment_decoder bcd_to_7_segment_decoder_5: pin names not known
  // Binary_to_BCD_converter #(.binvalue(8)) binary_to_bcd_converter_2: pin names not known; wires that end beside it: {rom_1_data_4, rom_1_data_3[0], rom_1_data, rom_1_data_2}
  // _7_Segment_Display 7_segment_display_6: pin names not known; wires that end beside it: n7_segment_display_6_p1, n7_segment_display_6_p1
  // BCD_to_7_Segment_decoder bcd_to_7_segment_decoder_6: pin names not known
  Decoder #(.select(3)) decoder_1 (
    .out1(decoder_1_out1), .out2(decoder_1_out2), .out3(decoder_1_out3), .out4(decoder_1_out4),
    .out5(decoder_1_out5), .out6(decoder_1_out6), .out7(decoder_1_out7), .sel({rom_1_data_3[0], rom_1_data}),
    .en(not_1_out));  // open: out0
  assign controlled_buffer_1_out = decoder_1_out1 ? dipswitch_1_sw8 : 8'bz;  // Controlled_Buffer controlled_buffer_1
  Decoder #(.select(3)) decoder_2 (
    .out1(decoder_2_out1), .out2(decoder_2_out2), .out3(decoder_2_out3), .out4(decoder_2_out4),
    .out5(decoder_2_out5), .out6(decoder_2_out6), .out7(decoder_2_out7), .sel(rom_1_data_2), .en(not_1_out));  // open: out0
  not not_1 (not_1_out, decoder_3_out2);
  Decoder #(.select(2)) decoder_3 (
    .out0(decoder_3_out0), .out1(decoder_3_out1), .out2(decoder_3_out2), .out3(decoder_3_out3),
    .sel(rom_1_data_4));  // open: en
  or or_1 (or_1_out, decoder_3_out0, decoder_2_out7);
  or or_2 (or_2_out, decoder_3_out1, decoder_2_out4);
  Register register_2 (.D(controlled_buffer_1_out), .en(1'b1), .clk(or_1_out), .Q(register_2_q));  // open: clr
  assign controlled_buffer_2_out = controlled_buffer_10_out ? register_2_q : 8'bz;  // Controlled_Buffer controlled_buffer_2
  Register register_3 (.D(controlled_buffer_1_out), .en(1'b1), .clk(decoder_2_out6), .Q(register_3_q));  // open: clr
  Register register_4 (.D(controlled_buffer_1_out), .en(1'b1), .clk(decoder_2_out5), .Q(register_4_q));  // open: clr
  Register register_5 (.D(controlled_buffer_1_out), .en(1'b1), .clk(or_2_out), .Q(register_5_q));  // open: clr
  Register register_6 (.D(controlled_buffer_1_out), .en(decoder_1_out3), .clk(decoder_2_out3));  // open: Q, clr
  Register register_7 (.D(controlled_buffer_1_out), .en(decoder_1_out2), .clk(decoder_2_out2));  // open: Q, clr
  assign controlled_buffer_1_out = decoder_3_out0 ? {rom_1_data_4, rom_1_data_3[0], rom_1_data, rom_1_data_2} : 8'bz;  // Controlled_Buffer controlled_buffer_3
  assign controlled_buffer_1_out = decoder_1_out7 ? register_2_q : 8'bz;  // Controlled_Buffer controlled_buffer_4
  assign controlled_buffer_1_out = decoder_1_out6 ? register_3_q : 8'bz;  // Controlled_Buffer controlled_buffer_5
  assign controlled_buffer_1_out = decoder_1_out5 ? register_4_q : 8'bz;  // Controlled_Buffer controlled_buffer_6
  assign controlled_buffer_1_out = decoder_1_out4 ? register_5_q : 8'bz;  // Controlled_Buffer controlled_buffer_7
  assign controlled_buffer_8_out = decoder_2_out1 ? controlled_buffer_1_out : 8'bz;  // Controlled_Buffer controlled_buffer_8
  // _7_Segment_Display 7_segment_display_7: pin names not known; wires that end beside it: n7_segment_display_7_p1, n7_segment_display_7_p1
  // BCD_to_7_Segment_decoder bcd_to_7_segment_decoder_7: pin names not known
  // Binary_to_BCD_converter #(.binvalue(8)) binary_to_bcd_converter_3: pin names not known; wires that end beside it: controlled_buffer_8_out
  // _7_Segment_Display 7_segment_display_8: pin names not known; wires that end beside it: n7_segment_display_8_p1, n7_segment_display_8_p1
  // BCD_to_7_Segment_decoder bcd_to_7_segment_decoder_8: pin names not known
  // _7_Segment_Display 7_segment_display_9: pin names not known; wires that end beside it: n7_segment_display_9_p1, n7_segment_display_9_p1
  // BCD_to_7_Segment_decoder bcd_to_7_segment_decoder_9: pin names not known
  assign controlled_buffer_1_out = decoder_3_out1 ? alu_1_aluoutput : 8'bz;  // Controlled_Buffer controlled_buffer_9
  ALU alu_1 (
    .Instruction({rom_1_data_4, rom_1_data_3[0]}), .Input1(register_3_q), .Input2(register_4_q),
    .ALUOutput(alu_1_aluoutput));
  singleNumberCond singlenumbercond_1 (
    .Condition({rom_1_data_4, rom_1_data_3[0]}), .Number(register_5_q), .Result(singlenumbercond_1_result));
  not not_2 (not_2_out, decoder_3_out3);
  assign controlled_buffer_10_out = not_2_out ? decoder_3_out3 : 1'bz;  // Controlled_Buffer controlled_buffer_10
  assign controlled_buffer_10_out = decoder_3_out3 ? singlenumbercond_1_result : 1'bz;  // Controlled_Buffer controlled_buffer_11

  // Notes on the sheet:
  //   contents of rom_1 (hex, n*v repeats v):
  //   6 d3 1
endmodule

module fullAdder (
  input  carryIn,
  input  num1,
  input  num2,
  output sum,
  output carryOut
);

  wire and_1_out, and_2_out, xor_1_out;

  xor xor_1 (xor_1_out, carryIn, num1);
  and and_1 (and_1_out, carryIn, num1);
  and and_2 (and_2_out, num2, xor_1_out);
  xor xor_2 (sum, xor_1_out, num2);
  or or_1 (carryOut, and_2_out, and_1_out);
endmodule

module eightBitAdder (
  input  carryIn,
  input  [7:0] input1,
  input  [7:0] input2,
  output [7:0] sum,
  output carryOut
);

  wire fulladder_1_carryout, fulladder_2_carryout, fulladder_3_carryout, fulladder_4_carryout,
       fulladder_5_carryout, fulladder_6_carryout, fulladder_7_carryout;

  fullAdder fulladder_1 (
    .carryIn(carryIn), .num1(input2[0]), .num2(input1[0]), .sum(sum[0]), .carryOut(fulladder_1_carryout));
  fullAdder fulladder_2 (
    .carryIn(fulladder_7_carryout), .num1(input2[4]), .num2(input1[4]), .sum(sum[4]),
    .carryOut(fulladder_2_carryout));
  fullAdder fulladder_3 (
    .carryIn(fulladder_1_carryout), .num1(input2[1]), .num2(input1[1]), .sum(sum[1]),
    .carryOut(fulladder_3_carryout));
  fullAdder fulladder_4 (
    .carryIn(fulladder_2_carryout), .num1(input2[5]), .num2(input1[5]), .sum(sum[5]),
    .carryOut(fulladder_4_carryout));
  fullAdder fulladder_5 (
    .carryIn(fulladder_3_carryout), .num1(input2[2]), .num2(input1[2]), .sum(sum[2]),
    .carryOut(fulladder_5_carryout));
  fullAdder fulladder_6 (
    .carryIn(fulladder_4_carryout), .num1(input2[6]), .num2(input1[6]), .sum(sum[6]),
    .carryOut(fulladder_6_carryout));
  fullAdder fulladder_7 (
    .carryIn(fulladder_5_carryout), .num1(input2[3]), .num2(input1[3]), .sum(sum[3]),
    .carryOut(fulladder_7_carryout));
  fullAdder fulladder_8 (
    .carryIn(fulladder_6_carryout), .num1(input2[7]), .num2(input1[7]), .sum(sum[7]), .carryOut(carryOut));
endmodule

module ALU (
  input  [2:0] Instruction,
  input  [7:0] Input1,
  input  [7:0] Input2,
  output [7:0] ALUOutput
);

  wire and_1_out, and_2_out, and_3_out, and_4_out, and_5_out, and_6_out, and_7_out, and_8_out,
       decoder_1_out0, decoder_1_out1, decoder_1_out2, decoder_1_out3, decoder_1_out4, decoder_1_out5,
       nand_1_out, nand_2_out, nand_3_out, nand_4_out, nand_5_out, nand_6_out, nand_7_out, nand_8_out,
       nor_1_out, nor_2_out, nor_3_out, nor_4_out, nor_5_out, nor_6_out, nor_7_out, nor_8_out, or_1_out,
       or_2_out, or_3_out, or_4_out, or_5_out, or_6_out, or_7_out, or_8_out;
  wire [7:0] eightbitadder_1_sum, eightbitadder_2_sum, not_1_out;

  Decoder #(.select(3)) decoder_1 (
    .out0(decoder_1_out0), .out1(decoder_1_out1), .out2(decoder_1_out2), .out3(decoder_1_out3),
    .out4(decoder_1_out4), .out5(decoder_1_out5), .sel(Instruction));  // open: out6, out7, en
  or or_1 (or_1_out, Input1[0], Input2[0]);
  assign ALUOutput[0] = decoder_1_out0 ? or_1_out : 1'bz;  // Controlled_Buffer controlled_buffer_1
  or or_2 (or_2_out, Input1[1], Input2[1]);
  assign ALUOutput[1] = decoder_1_out0 ? or_2_out : 1'bz;  // Controlled_Buffer controlled_buffer_2
  or or_3 (or_3_out, Input1[2], Input2[2]);
  assign ALUOutput[2] = decoder_1_out0 ? or_3_out : 1'bz;  // Controlled_Buffer controlled_buffer_3
  or or_4 (or_4_out, Input1[3], Input2[3]);
  assign ALUOutput[3] = decoder_1_out0 ? or_4_out : 1'bz;  // Controlled_Buffer controlled_buffer_4
  or or_5 (or_5_out, Input1[4], Input2[4]);
  assign ALUOutput[4] = decoder_1_out0 ? or_5_out : 1'bz;  // Controlled_Buffer controlled_buffer_5
  or or_6 (or_6_out, Input1[5], Input2[5]);
  assign ALUOutput[5] = decoder_1_out0 ? or_6_out : 1'bz;  // Controlled_Buffer controlled_buffer_6
  or or_7 (or_7_out, Input1[6], Input2[6]);
  assign ALUOutput[6] = decoder_1_out0 ? or_7_out : 1'bz;  // Controlled_Buffer controlled_buffer_7
  or or_8 (or_8_out, Input1[7], Input2[7]);
  assign ALUOutput[7] = decoder_1_out0 ? or_8_out : 1'bz;  // Controlled_Buffer controlled_buffer_8
  nand nand_1 (nand_1_out, Input1[0], Input2[0]);
  nand nand_2 (nand_2_out, Input1[1], Input2[1]);
  nand nand_3 (nand_3_out, Input1[2], Input2[2]);
  nand nand_4 (nand_4_out, Input1[3], Input2[3]);
  nand nand_5 (nand_5_out, Input1[4], Input2[4]);
  nand nand_6 (nand_6_out, Input1[5], Input2[5]);
  nand nand_7 (nand_7_out, Input1[6], Input2[6]);
  nand nand_8 (nand_8_out, Input1[7], Input2[7]);
  assign ALUOutput[0] = decoder_1_out1 ? nand_1_out : 1'bz;  // Controlled_Buffer controlled_buffer_9
  assign ALUOutput[1] = decoder_1_out1 ? nand_2_out : 1'bz;  // Controlled_Buffer controlled_buffer_10
  assign ALUOutput[2] = decoder_1_out1 ? nand_3_out : 1'bz;  // Controlled_Buffer controlled_buffer_11
  assign ALUOutput[3] = decoder_1_out1 ? nand_4_out : 1'bz;  // Controlled_Buffer controlled_buffer_12
  assign ALUOutput[4] = decoder_1_out1 ? nand_5_out : 1'bz;  // Controlled_Buffer controlled_buffer_13
  assign ALUOutput[5] = decoder_1_out1 ? nand_6_out : 1'bz;  // Controlled_Buffer controlled_buffer_14
  assign ALUOutput[6] = decoder_1_out1 ? nand_7_out : 1'bz;  // Controlled_Buffer controlled_buffer_15
  assign ALUOutput[7] = decoder_1_out1 ? nand_8_out : 1'bz;  // Controlled_Buffer controlled_buffer_16
  nor nor_1 (nor_1_out, Input1[0], Input2[0]);
  nor nor_2 (nor_2_out, Input1[1], Input2[1]);
  nor nor_3 (nor_3_out, Input1[2], Input2[2]);
  nor nor_4 (nor_4_out, Input1[3], Input2[3]);
  nor nor_5 (nor_5_out, Input1[4], Input2[4]);
  nor nor_6 (nor_6_out, Input1[5], Input2[5]);
  nor nor_7 (nor_7_out, Input1[6], Input2[6]);
  nor nor_8 (nor_8_out, Input1[7], Input2[7]);
  assign ALUOutput[0] = decoder_1_out2 ? nor_1_out : 1'bz;  // Controlled_Buffer controlled_buffer_17
  assign ALUOutput[1] = decoder_1_out2 ? nor_2_out : 1'bz;  // Controlled_Buffer controlled_buffer_18
  assign ALUOutput[2] = decoder_1_out2 ? nor_3_out : 1'bz;  // Controlled_Buffer controlled_buffer_19
  assign ALUOutput[3] = decoder_1_out2 ? nor_4_out : 1'bz;  // Controlled_Buffer controlled_buffer_20
  assign ALUOutput[4] = decoder_1_out2 ? nor_5_out : 1'bz;  // Controlled_Buffer controlled_buffer_21
  assign ALUOutput[5] = decoder_1_out2 ? nor_6_out : 1'bz;  // Controlled_Buffer controlled_buffer_22
  assign ALUOutput[6] = decoder_1_out2 ? nor_7_out : 1'bz;  // Controlled_Buffer controlled_buffer_23
  assign ALUOutput[7] = decoder_1_out2 ? nor_8_out : 1'bz;  // Controlled_Buffer controlled_buffer_24
  and and_1 (and_1_out, Input1[0], Input2[0]);
  and and_2 (and_2_out, Input1[1], Input2[1]);
  and and_3 (and_3_out, Input1[2], Input2[2]);
  and and_4 (and_4_out, Input1[3], Input2[3]);
  and and_5 (and_5_out, Input1[4], Input2[4]);
  and and_6 (and_6_out, Input1[5], Input2[5]);
  and and_7 (and_7_out, Input1[6], Input2[6]);
  and and_8 (and_8_out, Input1[7], Input2[7]);
  assign ALUOutput[0] = decoder_1_out3 ? and_1_out : 1'bz;  // Controlled_Buffer controlled_buffer_25
  assign ALUOutput[1] = decoder_1_out3 ? and_2_out : 1'bz;  // Controlled_Buffer controlled_buffer_26
  assign ALUOutput[2] = decoder_1_out3 ? and_3_out : 1'bz;  // Controlled_Buffer controlled_buffer_27
  assign ALUOutput[3] = decoder_1_out3 ? and_4_out : 1'bz;  // Controlled_Buffer controlled_buffer_28
  assign ALUOutput[4] = decoder_1_out3 ? and_5_out : 1'bz;  // Controlled_Buffer controlled_buffer_29
  assign ALUOutput[5] = decoder_1_out3 ? and_6_out : 1'bz;  // Controlled_Buffer controlled_buffer_30
  assign ALUOutput[6] = decoder_1_out3 ? and_7_out : 1'bz;  // Controlled_Buffer controlled_buffer_31
  assign ALUOutput[7] = decoder_1_out3 ? and_8_out : 1'bz;  // Controlled_Buffer controlled_buffer_32
  eightBitAdder eightbitadder_1 (
    .input1(Input1), .input2(Input2), .sum(eightbitadder_1_sum));  // open: carryIn, carryOut
  assign ALUOutput = decoder_1_out4 ? eightbitadder_1_sum : 8'bz;  // Controlled_Buffer controlled_buffer_33
  assign not_1_out = ~Input2;  // NOT_Gate not_1, 8 bits wide
  eightBitAdder eightbitadder_2 (
    .input1(Input1), .input2(not_1_out), .sum(eightbitadder_2_sum));  // open: carryIn, carryOut
  assign ALUOutput = decoder_1_out5 ? eightbitadder_2_sum : 8'bz;  // Controlled_Buffer controlled_buffer_34
endmodule

module singleNumberCond (
  input  [2:0] Condition,
  input  [7:0] Number,
  output Result
);

  wire decoder_1_out0, decoder_1_out1, decoder_1_out2, decoder_1_out3, decoder_1_out4, decoder_1_out5,
       decoder_1_out6, decoder_1_out7, nor_1_out, not_1_out, not_2_out, or_1_out, or_2_out, or_3_out,
       or_4_out, or_5_out, or_6_out, or_7_out, or_8_out, or_9_out;

  Decoder #(.select(3)) decoder_1 (
    .out0(decoder_1_out0), .out1(decoder_1_out1), .out2(decoder_1_out2), .out3(decoder_1_out3),
    .out4(decoder_1_out4), .out5(decoder_1_out5), .out6(decoder_1_out6), .out7(decoder_1_out7),
    .sel(Condition));  // open: en
  or or_1 (or_1_out, Number[0], Number[1]);
  or or_2 (or_2_out, Number[3], Number[4]);
  or or_3 (or_3_out, Number[6], Number[7]);
  or or_4 (or_4_out, or_1_out, Number[2]);
  or or_5 (or_5_out, or_4_out, or_6_out);
  or or_6 (or_6_out, or_2_out, Number[5]);
  or or_7 (or_7_out, or_5_out, or_3_out);
  not not_1 (not_1_out, Number[7]);
  assign Result = decoder_1_out5 ? or_7_out : 1'bz;  // Controlled_Buffer controlled_buffer_1
  not not_2 (not_2_out, or_7_out);
  or or_8 (or_8_out, not_2_out, Number[7]);
  or or_9 (or_9_out, not_2_out, not_1_out);
  assign Result = decoder_1_out1 ? not_2_out : 1'bz;  // Controlled_Buffer controlled_buffer_2
  assign Result = decoder_1_out6 ? or_9_out : 1'bz;  // Controlled_Buffer controlled_buffer_3
  nor nor_1 (nor_1_out, not_2_out, Number[7]);
  assign Result = decoder_1_out3 ? or_8_out : 1'bz;  // Controlled_Buffer controlled_buffer_4
  assign Result = decoder_1_out7 ? nor_1_out : 1'bz;  // Controlled_Buffer controlled_buffer_5
  assign Result = decoder_1_out4 ? decoder_1_out4 : 1'bz;  // Controlled_Buffer controlled_buffer_6
  assign Result = decoder_1_out2 ? Number[7] : 1'bz;  // Controlled_Buffer controlled_buffer_7

  // Notes on the sheet:
  //   never
  //   OR all bits
  //   != 0
  //   = 0
  //   < 0
  //   > 0
  //   < 0
  //   = 0
  //   <= 0
  //   >= 0
  //   < 0
  //   always
endmodule
