// Logisim project FLIP8_TTL.circ as structural Verilog: 3 circuits, main circuit main
module main (
  input  [2:0] in_1,
  input  [7:0] in_2,
  input  [7:0] in_3
);

  wire CKL, Compute, Condition, Copy, COUNT_OWR, Immediate, loadIN, loadREG0, loadREG1, loadREG2, loadREG3,
       loadREG4, loadREG5, n7_segment_display_1_p1, n7_segment_display_2_p1, n7_segment_display_3_p1,
       n7_segment_display_4_p1, n7_segment_display_5_p1, n7_segment_display_6_p1, n7_segment_display_7_p1,
       n7_segment_display_8_p1, n7_segment_display_9_p1, n7404_2_pin12, n7436_1_pin1, n7436_1_pin2,
       n7436_1_pin3, n7436_1_pin4, n7436_1_pin5, n7436_1_pin6, n74125_1_pin3, n74138_1_pin6, n74138_1_pin8,
       n74138_2_pin6, n74138_2_pin8, n74138_3_pin4, n74138_3_pin6, n74161_1_pin1, n74161_1_pin7,
       n74161_1_pin8, n74161_1_pin10, n74161_1_pin16, n74161_2_pin8, n74240_1_pin1, n74240_1_pin2,
       n74240_1_pin3, n74240_1_pin4, n74240_1_pin5, n74240_1_pin6, n74240_1_pin7, n74240_1_pin8,
       n74240_1_pin9, n74240_1_pin11, n74240_1_pin12, n74240_1_pin13, n74240_1_pin14, n74240_1_pin15,
       n74240_1_pin16, n74240_1_pin17, n74240_1_pin18, n74240_2_pin2, n74240_2_pin3, n74240_2_pin4,
       n74240_2_pin5, n74240_2_pin6, n74240_2_pin7, n74240_2_pin8, n74240_2_pin9, n74240_2_pin11,
       n74240_2_pin12, n74240_2_pin13, n74240_2_pin14, n74240_2_pin15, n74240_2_pin16, n74240_2_pin17,
       n74240_2_pin18, n74244_2_pin2, n74244_2_pin4, n74244_2_pin6, n74244_2_pin8, n74244_2_pin11,
       n74244_2_pin13, n74244_2_pin15, n74244_2_pin17, n74377_1_pin2, n74377_1_pin3, n74377_1_pin4,
       n74377_1_pin5, n74377_1_pin6, n74377_1_pin7, n74377_1_pin8, n74377_1_pin9, n74377_1_pin12,
       n74377_1_pin13, n74377_1_pin14, n74377_1_pin15, n74377_1_pin16, n74377_1_pin17, n74377_1_pin18,
       n74377_1_pin19, n74377_2_pin2, n74377_2_pin5, n74377_2_pin6, n74377_2_pin9, n74377_2_pin12,
       n74377_2_pin15, n74377_2_pin16, n74377_2_pin19, not_1_out, RESET, saveREG0, saveREG1, saveREG2,
       saveREG3, saveREG4, saveREG5, singlenumbercond_1_result, toOut;
  wire [7:0] alu_1_out_4, alu_2_out_4, n74161_2_pin3, n74161_2_pin14, n74244_3_pin17, n74244_4_pin17,
       n74244_5_pin17, rom_1_data;

  Button button_1 (.out(COUNT_OWR));
  Button button_2 (.out(RESET));
  Clock clock_1 (.out(CKL));
  _74240 #(.ShowInternalStructure("true")) u_74240_1 (
    .pin1(n74240_1_pin1), .pin2(n74240_1_pin2), .pin3(n74240_1_pin3), .pin4(n74240_1_pin4),
    .pin5(n74240_1_pin5), .pin6(n74240_1_pin6), .pin7(n74240_1_pin7), .pin8(n74240_1_pin8),
    .pin9(n74240_1_pin9), .pin19(n74240_1_pin1), .pin18(n74240_1_pin18), .pin17(n74240_1_pin17),
    .pin16(n74240_1_pin16), .pin15(n74240_1_pin15), .pin14(n74240_1_pin14), .pin13(n74240_1_pin13),
    .pin12(n74240_1_pin12), .pin11(n74240_1_pin11));
  not not_1 (not_1_out, COUNT_OWR);
  _74161 #(.ShowInternalStructure("true"), .VccGndPorts("true")) u_74161_1 (
    .pin1(n74161_1_pin1), .pin2(CKL), .pin3(n74161_2_pin3[4]), .pin4(n74161_2_pin3[5]),
    .pin5(n74161_2_pin3[6]), .pin6(n74161_2_pin3[7]), .pin7(n74161_1_pin7), .pin8(n74161_1_pin8),
    .pin16(n74161_1_pin16), .pin14(n74161_2_pin14[4]), .pin13(n74161_2_pin14[5]), .pin12(n74161_2_pin14[6]),
    .pin11(n74161_2_pin14[7]), .pin10(n74161_1_pin10), .pin9(not_1_out));  // open: pin15
  not not_2 (n74161_1_pin1, RESET);
  _74240 #(.ShowInternalStructure("true")) u_74240_2 (
    .pin1(n74240_1_pin1), .pin2(n74240_2_pin2), .pin3(n74240_2_pin3), .pin4(n74240_2_pin4),
    .pin5(n74240_2_pin5), .pin6(n74240_2_pin6), .pin7(n74240_2_pin7), .pin8(n74240_2_pin8),
    .pin9(n74240_2_pin9), .pin19(n74240_1_pin1), .pin18(n74240_2_pin18), .pin17(n74240_2_pin17),
    .pin16(n74240_2_pin16), .pin15(n74240_2_pin15), .pin14(n74240_2_pin14), .pin13(n74240_2_pin13),
    .pin12(n74240_2_pin12), .pin11(n74240_2_pin11));
  _74161 #(.ShowInternalStructure("true"), .VccGndPorts("true")) u_74161_2 (
    .pin1(n74161_1_pin1), .pin2(CKL), .pin3(n74161_2_pin3[0]), .pin4(n74161_2_pin3[1]),
    .pin5(n74161_2_pin3[2]), .pin6(n74161_2_pin3[3]), .pin7(n74161_1_pin7), .pin8(n74161_2_pin8),
    .pin16(n74161_1_pin7), .pin15(n74161_1_pin10), .pin14(n74161_2_pin14[0]), .pin13(n74161_2_pin14[1]),
    .pin12(n74161_2_pin14[2]), .pin11(n74161_2_pin14[3]), .pin10(n74161_1_pin7), .pin9(not_1_out));
  // _7_Segment_Display 7_segment_display_1: pin names not known; wires that end beside it: n7_segment_display_1_p1, n7_segment_display_1_p1
  // BCD_to_7_Segment_decoder bcd_to_7_segment_decoder_1: pin names not known
  // Binary_to_BCD_converter #(.binvalue(8)) binary_to_bcd_converter_1: pin names not known; wires that end beside it: n74161_2_pin14
  // _7_Segment_Display 7_segment_display_2: pin names not known; wires that end beside it: n7_segment_display_2_p1, n7_segment_display_2_p1
  // BCD_to_7_Segment_decoder bcd_to_7_segment_decoder_2: pin names not known
  ALU alu_1 (.Instruction(in_1), .Input1(in_2), .Input2(in_3), .out_4(alu_1_out_4));
  // _7_Segment_Display 7_segment_display_3: pin names not known; wires that end beside it: n7_segment_display_3_p1, n7_segment_display_3_p1
  // _7_Segment_Display 7_segment_display_4: pin names not known; wires that end beside it: n7_segment_display_4_p1, n7_segment_display_4_p1
  // BCD_to_7_Segment_decoder bcd_to_7_segment_decoder_3: pin names not known
  // BCD_to_7_Segment_decoder bcd_to_7_segment_decoder_4: pin names not known
  ROM rom_1 (.addr(n74161_2_pin14), .data(rom_1_data));
  // _7_Segment_Display 7_segment_display_5: pin names not known; wires that end beside it: n7_segment_display_5_p1, n7_segment_display_5_p1
  // BCD_to_7_Segment_decoder bcd_to_7_segment_decoder_5: pin names not known
  // Binary_to_BCD_converter #(.binvalue(8)) binary_to_bcd_converter_2: pin names not known; wires that end beside it: alu_1_out_4
  // _7_Segment_Display 7_segment_display_6: pin names not known; wires that end beside it: n7_segment_display_6_p1, n7_segment_display_6_p1
  // BCD_to_7_Segment_decoder bcd_to_7_segment_decoder_6: pin names not known
  LedBar ledbar_1 (
    .led0(rom_1_data[7]), .led1(rom_1_data[6]), .led2(rom_1_data[5]), .led3(rom_1_data[4]),
    .led4(rom_1_data[3]), .led5(rom_1_data[2]), .led6(rom_1_data[1]), .led7(rom_1_data[0]));
  _74138 #(.ShowInternalStructure("true"), .VccGndPorts("true")) u_74138_1 (
    .pin1(rom_1_data[3]), .pin2(rom_1_data[4]), .pin3(rom_1_data[5]), .pin4(Copy), .pin5(Copy),
    .pin6(n74138_1_pin6), .pin8(n74138_1_pin8), .pin16(n74138_1_pin6), .pin15(loadREG0), .pin14(loadREG1),
    .pin13(loadREG2), .pin12(loadREG3), .pin11(loadREG4), .pin10(loadREG5), .pin9(loadIN));  // open: pin7
  _74138 #(.ShowInternalStructure("true"), .VccGndPorts("true")) u_74138_2 (
    .pin1(rom_1_data[0]), .pin2(rom_1_data[1]), .pin3(rom_1_data[2]), .pin4(Copy), .pin5(Copy),
    .pin6(n74138_2_pin6), .pin8(n74138_2_pin8), .pin16(n74138_2_pin6), .pin15(saveREG0), .pin14(saveREG1),
    .pin13(saveREG2), .pin12(saveREG3), .pin11(saveREG4), .pin10(saveREG5), .pin9(toOut));  // open: pin7
  _74377 #(.ShowInternalStructure("true")) u_74377_1 (
    .pin1(saveREG4), .pin2(n74377_1_pin2), .pin3(n74377_1_pin3), .pin4(n74377_1_pin4), .pin5(n74377_1_pin5),
    .pin6(n74377_1_pin6), .pin7(n74377_1_pin7), .pin8(n74377_1_pin8), .pin9(n74377_1_pin9),
    .pin19(n74377_1_pin19), .pin18(n74377_1_pin18), .pin17(n74377_1_pin17), .pin16(n74377_1_pin16),
    .pin15(n74377_1_pin15), .pin14(n74377_1_pin14), .pin13(n74377_1_pin13), .pin12(n74377_1_pin12),
    .pin11(CKL));
  _74377 #(.ShowInternalStructure("true")) u_74377_2 (
    .pin1(saveREG5), .pin2(n74377_2_pin2), .pin3(n74377_1_pin3), .pin4(n74377_1_pin4), .pin5(n74377_2_pin5),
    .pin6(n74377_2_pin6), .pin7(n74377_1_pin7), .pin8(n74377_1_pin8), .pin9(n74377_2_pin9),
    .pin19(n74377_2_pin19), .pin18(n74377_1_pin18), .pin17(n74377_1_pin17), .pin16(n74377_2_pin16),
    .pin15(n74377_2_pin15), .pin14(n74377_1_pin14), .pin13(n74377_1_pin13), .pin12(n74377_2_pin12),
    .pin11(CKL));
  _74138 #(.ShowInternalStructure("true"), .VccGndPorts("true")) u_74138_3 (
    .pin1(rom_1_data[6]), .pin2(rom_1_data[7]), .pin4(n74138_3_pin4), .pin5(n74138_3_pin4),
    .pin6(n74138_3_pin6), .pin8(n74138_3_pin4), .pin16(n74138_3_pin6), .pin15(Immediate), .pin14(Compute),
    .pin13(Copy), .pin12(Condition));  // open: pin3, pin7, pin11, pin10, pin9
  _74244 #(.ShowInternalStructure("true")) u_74244_1 (
    .pin1(loadREG4), .pin2(n74377_1_pin9), .pin3(n74377_1_pin13), .pin4(n74377_1_pin6),
    .pin5(n74377_1_pin14), .pin6(n74377_1_pin5), .pin7(n74377_1_pin17), .pin8(n74377_1_pin2),
    .pin9(n74377_1_pin18), .pin19(loadREG4), .pin18(n74377_1_pin8), .pin17(n74377_1_pin12),
    .pin16(n74377_1_pin7), .pin15(n74377_1_pin15), .pin14(n74377_1_pin4), .pin13(n74377_1_pin16),
    .pin12(n74377_1_pin3), .pin11(n74377_1_pin19));
  _74240 #(.ShowInternalStructure("true")) u_74240_3 (
    .pin1(loadREG5), .pin2(n74377_2_pin9), .pin3(n74377_1_pin13), .pin4(n74377_2_pin6),
    .pin5(n74377_1_pin14), .pin6(n74377_2_pin5), .pin7(n74377_1_pin17), .pin8(n74377_2_pin2),
    .pin9(n74377_1_pin18), .pin19(loadREG5), .pin18(n74377_1_pin8), .pin17(n74377_2_pin12),
    .pin16(n74377_1_pin7), .pin15(n74377_2_pin15), .pin14(n74377_1_pin4), .pin13(n74377_2_pin16),
    .pin12(n74377_1_pin3), .pin11(n74377_2_pin19));
  _74240 #(.ShowInternalStructure("true")) u_74240_4 (
    .pin1(Immediate), .pin2(rom_1_data[3]), .pin3(n74377_1_pin18), .pin4(rom_1_data[2]),
    .pin5(n74377_1_pin17), .pin6(rom_1_data[1]), .pin7(n74377_1_pin14), .pin8(rom_1_data[0]),
    .pin9(n74377_1_pin13), .pin19(Immediate), .pin18(n74377_1_pin8), .pin17(rom_1_data[7]),
    .pin16(n74377_1_pin7), .pin15(rom_1_data[6]), .pin14(n74377_1_pin4), .pin13(rom_1_data[5]),
    .pin12(n74377_1_pin3), .pin11(rom_1_data[4]));
  _7436 #(.ShowInternalStructure("true")) u_7436_1 (
    .pin1(n7436_1_pin1), .pin2(n7436_1_pin2), .pin3(n7436_1_pin3), .pin4(n7436_1_pin4), .pin5(n7436_1_pin5),
    .pin6(n7436_1_pin6));  // open: pin13, pin12, pin11, pin10, pin9, pin8
  _74244 #(.ShowInternalStructure("true")) u_74244_2 (
    .pin1(loadREG0), .pin2(n74244_2_pin2), .pin3(n74377_1_pin3), .pin4(n74244_2_pin4), .pin5(n74377_1_pin4),
    .pin6(n74244_2_pin6), .pin7(n74377_1_pin7), .pin8(n74244_2_pin8), .pin9(n74377_1_pin8), .pin19(loadREG0),
    .pin18(n74377_1_pin18), .pin17(n74244_2_pin17), .pin16(n74377_1_pin17), .pin15(n74244_2_pin15),
    .pin14(n74377_1_pin14), .pin13(n74244_2_pin13), .pin12(n74377_1_pin13), .pin11(n74244_2_pin11));
  _74244 #(.ShowInternalStructure("true")) u_74244_3 (
    .pin1(loadREG1), .pin2(n74244_3_pin17[7]), .pin3(n74377_1_pin3), .pin4(n74244_3_pin17[6]),
    .pin5(n74377_1_pin4), .pin6(n74244_3_pin17[5]), .pin7(n74377_1_pin7), .pin8(n74244_3_pin17[4]),
    .pin9(n74377_1_pin8), .pin19(loadREG1), .pin18(n74377_1_pin18), .pin17(n74244_3_pin17[0]),
    .pin16(n74377_1_pin17), .pin15(n74244_3_pin17[1]), .pin14(n74377_1_pin14), .pin13(n74244_3_pin17[2]),
    .pin12(n74377_1_pin13), .pin11(n74244_3_pin17[3]));
  _74244 #(.ShowInternalStructure("true")) u_74244_4 (
    .pin1(loadREG2), .pin2(n74244_4_pin17[7]), .pin3(n74377_1_pin3), .pin4(n74244_4_pin17[6]),
    .pin5(n74377_1_pin4), .pin6(n74244_4_pin17[5]), .pin7(n74377_1_pin7), .pin8(n74244_4_pin17[4]),
    .pin9(n74377_1_pin8), .pin19(loadREG2), .pin18(n74377_1_pin18), .pin17(n74244_4_pin17[0]),
    .pin16(n74377_1_pin17), .pin15(n74244_4_pin17[1]), .pin14(n74377_1_pin14), .pin13(n74244_4_pin17[2]),
    .pin12(n74377_1_pin13), .pin11(n74244_4_pin17[3]));
  _74244 #(.ShowInternalStructure("true")) u_74244_5 (
    .pin1(loadREG3), .pin2(n74244_5_pin17[7]), .pin3(n74377_1_pin3), .pin4(n74244_5_pin17[6]),
    .pin5(n74377_1_pin4), .pin6(n74244_5_pin17[5]), .pin7(n74377_1_pin7), .pin8(n74244_5_pin17[4]),
    .pin9(n74377_1_pin8), .pin19(loadREG3), .pin18(n74377_1_pin18), .pin17(n74244_5_pin17[0]),
    .pin16(n74377_1_pin17), .pin15(n74244_5_pin17[1]), .pin14(n74377_1_pin14), .pin13(n74244_5_pin17[2]),
    .pin12(n74377_1_pin13), .pin11(n74244_5_pin17[3]));
  // _7_Segment_Display 7_segment_display_7: pin names not known; wires that end beside it: n7_segment_display_7_p1, n7_segment_display_7_p1
  // _7_Segment_Display 7_segment_display_8: pin names not known; wires that end beside it: n7_segment_display_8_p1, n7_segment_display_8_p1
  // BCD_to_7_Segment_decoder bcd_to_7_segment_decoder_7: pin names not known
  // BCD_to_7_Segment_decoder bcd_to_7_segment_decoder_8: pin names not known
  // Binary_to_BCD_converter #(.binvalue(8)) binary_to_bcd_converter_3: pin names not known; wires that end beside it: rom_1_data
  _74377 #(.ShowInternalStructure("true")) u_74377_3 (
    .pin1(n7436_1_pin3), .pin2(n74244_2_pin17), .pin3(n74377_1_pin3), .pin4(n74377_1_pin4),
    .pin5(n74244_2_pin15), .pin6(n74244_2_pin13), .pin7(n74377_1_pin7), .pin8(n74377_1_pin8),
    .pin9(n74244_2_pin11), .pin19(n74244_2_pin2), .pin18(n74377_1_pin18), .pin17(n74377_1_pin17),
    .pin16(n74244_2_pin4), .pin15(n74244_2_pin6), .pin14(n74377_1_pin14), .pin13(n74377_1_pin13),
    .pin12(n74244_2_pin8), .pin11(CKL));
  _74377 #(.ShowInternalStructure("true")) u_74377_4 (
    .pin1(saveREG1), .pin2(n74244_3_pin17[0]), .pin3(n74377_1_pin3), .pin4(n74377_1_pin4),
    .pin5(n74244_3_pin17[1]), .pin6(n74244_3_pin17[2]), .pin7(n74377_1_pin7), .pin8(n74377_1_pin8),
    .pin9(n74244_3_pin17[3]), .pin19(n74244_3_pin17[7]), .pin18(n74377_1_pin18), .pin17(n74377_1_pin17),
    .pin16(n74244_3_pin17[6]), .pin15(n74244_3_pin17[5]), .pin14(n74377_1_pin14), .pin13(n74377_1_pin13),
    .pin12(n74244_3_pin17[4]), .pin11(CKL));
  _74377 #(.ShowInternalStructure("true")) u_74377_5 (
    .pin1(saveREG2), .pin2(n74244_4_pin17[0]), .pin3(n74377_1_pin3), .pin4(n74377_1_pin4),
    .pin5(n74244_4_pin17[1]), .pin6(n74244_4_pin17[2]), .pin7(n74377_1_pin7), .pin8(n74377_1_pin8),
    .pin9(n74244_4_pin17[3]), .pin19(n74244_4_pin17[7]), .pin18(n74377_1_pin18), .pin17(n74377_1_pin17),
    .pin16(n74244_4_pin17[6]), .pin15(n74244_4_pin17[5]), .pin14(n74377_1_pin14), .pin13(n74377_1_pin13),
    .pin12(n74244_4_pin17[4]), .pin11(CKL));
  _74377 #(.ShowInternalStructure("true")) u_74377_6 (
    .pin1(n7436_1_pin6), .pin2(n74244_5_pin17[0]), .pin3(n74377_1_pin3), .pin4(n74377_1_pin4),
    .pin5(n74244_5_pin17[1]), .pin6(n74244_5_pin17[2]), .pin7(n74377_1_pin7), .pin8(n74377_1_pin8),
    .pin9(n74244_5_pin17[3]), .pin19(n74244_5_pin17[7]), .pin18(n74377_1_pin18), .pin17(n74377_1_pin17),
    .pin16(n74244_5_pin17[6]), .pin15(n74244_5_pin17[5]), .pin14(n74377_1_pin14), .pin13(n74377_1_pin13),
    .pin12(n74244_5_pin17[4]), .pin11(CKL));
  // _7_Segment_Display 7_segment_display_9: pin names not known; wires that end beside it: n7_segment_display_9_p1, n7_segment_display_9_p1
  // BCD_to_7_Segment_decoder bcd_to_7_segment_decoder_9: pin names not known
  _7404 #(.ShowInternalStructure("true")) u_7404_1 (
    .pin3(saveREG3), .pin4(n7436_1_pin4), .pin5(Compute), .pin6(n7436_1_pin5), .pin13(saveREG0),
    .pin12(n7436_1_pin1), .pin11(Immediate), .pin10(n7436_1_pin2));  // open: pin1, pin2, pin9, pin8
  _7404 #(.ShowInternalStructure("true")) u_7404_2 (
    .pin13(Condition), .pin12(n7404_2_pin12));  // open: pin1, pin2, pin3, pin4, pin5, pin6, pin11, pin10, pin9, pin8
  ALU alu_2 (.Instruction(rom_1_data[2:0]), .Input1(n74244_3_pin17), .Input2(n74244_4_pin17), .out_4(alu_2_out_4));
  singleNumberCond singlenumbercond_1 (
    .Condition(rom_1_data[2:0]), .Number(n74244_5_pin17), .Result(singlenumbercond_1_result));
  _74125 #(.ShowInternalStructure("true")) u_74125_1 (
    .pin1(Condition), .pin2(singlenumbercond_1_result), .pin3(n74125_1_pin3), .pin4(n7404_2_pin12),
    .pin5(Condition), .pin6(n74125_1_pin3));  // open: pin13, pin12, pin11, pin10, pin9, pin8
  _74244 #(.ShowInternalStructure("true")) u_74244_6 (
    .pin1(Compute), .pin2(alu_2_out_4[4]), .pin3(n74377_1_pin3), .pin4(alu_2_out_4[5]), .pin5(n74377_1_pin4),
    .pin6(alu_2_out_4[6]), .pin7(n74377_1_pin7), .pin8(alu_2_out_4[7]), .pin9(n74377_1_pin8),
    .pin19(Compute), .pin18(n74377_1_pin13), .pin17(alu_2_out_4[0]), .pin16(n74377_1_pin14),
    .pin15(alu_2_out_4[1]), .pin14(n74377_1_pin17), .pin13(alu_2_out_4[2]), .pin12(n74377_1_pin18),
    .pin11(alu_2_out_4[3]));
  // also tied to GND on the sheet: {n74161_1_pin8, n74161_2_pin8, n74138_1_pin8, n74138_2_pin8, n74138_3_pin4}
  // also tied to VCC on the sheet: {n74161_1_pin16, n74161_1_pin7, n74138_1_pin6, n74138_2_pin6, n74138_3_pin6}

  // Notes on the sheet:
  //   contents of rom_1 (hex, n*v repeats v):
  //   20 81 8a 93 9c a5
endmodule

module ALU (
  input  [2:0] Instruction,
  input  [7:0] Input1,
  input  [7:0] Input2,
  output [7:0] out_4
);

  wire EN_ADD, EN_AND, EN_NAND, EN_NOR, EN_OR, EN_SUB, n7400_1_pin3, n7400_1_pin6, n7400_1_pin8,
       n7400_1_pin11, n7400_2_pin3, n7400_2_pin6, n7400_2_pin8, n7400_2_pin11, n7402_1_pin1, n7402_1_pin4,
       n7402_1_pin10, n7402_1_pin13, n7402_2_pin1, n7402_2_pin4, n7402_2_pin10, n7402_2_pin13, n7404_1_pin8,
       n7408_1_pin3, n7408_1_pin6, n7408_1_pin8, n7408_1_pin11, n7408_2_pin3, n7408_2_pin6, n7408_2_pin8,
       n7408_2_pin11, n7432_1_pin3, n7432_1_pin6, n7432_1_pin8, n7432_1_pin11, n7432_2_pin3, n7432_2_pin6,
       n7432_2_pin8, n7432_2_pin11, n7436_1_pin3, n74138_1_pin4, n74138_1_pin6, n74283_1_pin1, n74283_1_pin3,
       n74283_1_pin4, n74283_1_pin5, n74283_1_pin7, n74283_1_pin9, n74283_1_pin10, n74283_1_pin12,
       n74283_1_pin13, n74283_1_pin14, n74283_2_pin1, n74283_2_pin3, n74283_2_pin4, n74283_2_pin5,
       n74283_2_pin10, n74283_2_pin12, n74283_2_pin13, n74283_2_pin15;

  _7432 #(.ShowInternalStructure("true")) u_7432_1 (
    .pin1(Input1[3]), .pin2(Input2[3]), .pin3(n7432_1_pin3), .pin4(Input1[2]), .pin5(Input2[2]),
    .pin6(n7432_1_pin6), .pin13(Input1[7]), .pin12(Input2[7]), .pin11(n7432_1_pin11), .pin10(Input1[6]),
    .pin9(Input2[6]), .pin8(n7432_1_pin8));
  _7432 #(.ShowInternalStructure("true")) u_7432_2 (
    .pin1(Input1[1]), .pin2(Input2[1]), .pin3(n7432_2_pin3), .pin4(Input1[0]), .pin5(Input2[0]),
    .pin6(n7432_2_pin6), .pin13(Input1[5]), .pin12(Input2[5]), .pin11(n7432_2_pin11), .pin10(Input1[4]),
    .pin9(Input2[4]), .pin8(n7432_2_pin8));
  _7402 #(.ShowInternalStructure("true")) u_7402_1 (
    .pin1(n7402_1_pin1), .pin2(Input2[6]), .pin3(Input1[6]), .pin4(n7402_1_pin4), .pin5(Input2[7]),
    .pin6(Input1[7]), .pin13(n7402_1_pin13), .pin12(Input2[2]), .pin11(Input1[2]), .pin10(n7402_1_pin10),
    .pin9(Input2[3]), .pin8(Input1[3]));
  _74138 #(.ShowInternalStructure("true"), .VccGndPorts("true")) u_74138_1 (
    .pin1(Instruction[0]), .pin2(Instruction[1]), .pin3(Instruction[2]), .pin4(n74138_1_pin4),
    .pin5(n74138_1_pin4), .pin6(n74138_1_pin6), .pin8(n74138_1_pin4), .pin16(n74138_1_pin6), .pin15(EN_OR),
    .pin14(EN_NAND), .pin13(EN_NOR), .pin12(EN_AND), .pin11(EN_ADD), .pin10(EN_SUB));  // open: pin7, pin9
  _7402 #(.ShowInternalStructure("true")) u_7402_2 (
    .pin1(n7402_2_pin1), .pin2(Input2[4]), .pin3(Input1[4]), .pin4(n7402_2_pin4), .pin5(Input2[5]),
    .pin6(Input1[5]), .pin13(n7402_2_pin13), .pin12(Input2[0]), .pin11(Input1[0]), .pin10(n7402_2_pin10),
    .pin9(Input2[1]), .pin8(Input1[1]));
  _74244 #(.ShowInternalStructure("true")) u_74244_1 (
    .pin1(EN_OR), .pin2(n7432_1_pin11), .pin3(out_4[3]), .pin4(n7432_1_pin8), .pin5(out_4[2]),
    .pin6(n7432_2_pin11), .pin7(out_4[1]), .pin8(n7432_2_pin8), .pin9(out_4[0]), .pin19(EN_OR),
    .pin18(out_4[7]), .pin17(n7432_1_pin3), .pin16(out_4[6]), .pin15(n7432_1_pin6), .pin14(out_4[5]),
    .pin13(n7432_2_pin3), .pin12(out_4[4]), .pin11(n7432_2_pin6));
  _74244 #(.ShowInternalStructure("true")) u_74244_2 (
    .pin1(EN_NOR), .pin2(n7402_1_pin4), .pin3(out_4[3]), .pin4(n7402_1_pin1), .pin5(out_4[2]),
    .pin6(n7402_2_pin4), .pin7(out_4[1]), .pin8(n7402_2_pin1), .pin9(out_4[0]), .pin19(EN_NOR),
    .pin18(out_4[7]), .pin17(n7402_1_pin10), .pin16(out_4[6]), .pin15(n7402_1_pin13), .pin14(out_4[5]),
    .pin13(n7402_2_pin10), .pin12(out_4[4]), .pin11(n7402_2_pin13));
  _7400 #(.ShowInternalStructure("true")) u_7400_1 (
    .pin1(Input1[3]), .pin2(Input2[3]), .pin3(n7400_1_pin3), .pin4(Input1[2]), .pin5(Input2[2]),
    .pin6(n7400_1_pin6), .pin13(Input1[7]), .pin12(Input2[7]), .pin11(n7400_1_pin11), .pin10(Input1[6]),
    .pin9(Input2[6]), .pin8(n7400_1_pin8));
  _7408 #(.ShowInternalStructure("true")) u_7408_1 (
    .pin1(Input1[3]), .pin2(Input2[3]), .pin3(n7408_1_pin3), .pin4(Input1[2]), .pin5(Input2[2]),
    .pin6(n7408_1_pin6), .pin13(Input1[7]), .pin12(Input2[7]), .pin11(n7408_1_pin11), .pin10(Input1[6]),
    .pin9(Input2[6]), .pin8(n7408_1_pin8));
  _7400 #(.ShowInternalStructure("true")) u_7400_2 (
    .pin1(Input1[1]), .pin2(Input2[1]), .pin3(n7400_2_pin3), .pin4(Input1[0]), .pin5(Input2[0]),
    .pin6(n7400_2_pin6), .pin13(Input1[5]), .pin12(Input2[5]), .pin11(n7400_2_pin11), .pin10(Input1[4]),
    .pin9(Input2[4]), .pin8(n7400_2_pin8));
  _7408 #(.ShowInternalStructure("true")) u_7408_2 (
    .pin1(Input1[1]), .pin2(Input2[1]), .pin3(n7408_2_pin3), .pin4(Input1[0]), .pin5(Input2[0]),
    .pin6(n7408_2_pin6), .pin13(Input1[5]), .pin12(Input2[5]), .pin11(n7408_2_pin11), .pin10(Input1[4]),
    .pin9(Input2[4]), .pin8(n7408_2_pin8));
  _74244 #(.ShowInternalStructure("true")) u_74244_3 (
    .pin1(EN_NAND), .pin2(n7400_1_pin11), .pin3(out_4[3]), .pin4(n7400_1_pin8), .pin5(out_4[2]),
    .pin6(n7400_2_pin11), .pin7(out_4[1]), .pin8(n7400_2_pin8), .pin9(out_4[0]), .pin19(EN_NAND),
    .pin18(out_4[7]), .pin17(n7400_1_pin3), .pin16(out_4[6]), .pin15(n7400_1_pin6), .pin14(out_4[5]),
    .pin13(n7400_2_pin3), .pin12(out_4[4]), .pin11(n7400_2_pin6));
  _74244 #(.ShowInternalStructure("true")) u_74244_4 (
    .pin1(EN_AND), .pin2(n7408_1_pin11), .pin3(out_4[3]), .pin4(n7408_1_pin8), .pin5(out_4[2]),
    .pin6(n7408_2_pin11), .pin7(out_4[1]), .pin8(n7408_2_pin8), .pin9(out_4[0]), .pin19(EN_AND),
    .pin18(out_4[7]), .pin17(n7408_1_pin3), .pin16(out_4[6]), .pin15(n7408_1_pin6), .pin14(out_4[5]),
    .pin13(n7408_2_pin3), .pin12(out_4[4]), .pin11(n7408_2_pin6));
  _74283 #(.ShowInternalStructure("true")) u_74283_1 (
    .pin1(n74283_1_pin1), .pin2(Input1[1]), .pin3(n74283_1_pin3), .pin4(n74283_1_pin4), .pin5(n74283_1_pin5),
    .pin6(Input1[0]), .pin7(n74283_1_pin7), .pin15(Input1[2]), .pin14(n74283_1_pin14),
    .pin13(n74283_1_pin13), .pin12(n74283_1_pin12), .pin11(Input1[3]), .pin10(n74283_1_pin10),
    .pin9(n74283_1_pin9));
  _74283 #(.ShowInternalStructure("true")) u_74283_2 (
    .pin1(n74283_2_pin1), .pin2(Input1[5]), .pin3(n74283_2_pin3), .pin4(n74283_2_pin4), .pin5(n74283_2_pin5),
    .pin6(Input1[4]), .pin7(n74283_1_pin9), .pin15(n74283_2_pin15), .pin14(Input1[6]),
    .pin13(n74283_2_pin13), .pin12(n74283_2_pin12), .pin11(Input1[7]), .pin10(n74283_2_pin10));  // open: pin9
  _7486 #(.ShowInternalStructure("true")) u_7486_1 (
    .pin1(Input2[5]), .pin2(n74283_1_pin7), .pin3(n74283_2_pin3), .pin4(Input2[4]), .pin5(n74283_1_pin7),
    .pin6(n74283_2_pin5), .pin13(Input2[6]), .pin12(n74283_1_pin7), .pin11(n74283_2_pin15),
    .pin10(Input2[7]), .pin9(n74283_1_pin7), .pin8(n74283_2_pin12));
  _7486 #(.ShowInternalStructure("true")) u_7486_2 (
    .pin1(Input2[1]), .pin2(n74283_1_pin7), .pin3(n74283_1_pin3), .pin4(Input2[0]), .pin5(n74283_1_pin7),
    .pin6(n74283_1_pin5), .pin13(Input2[2]), .pin12(n74283_1_pin7), .pin11(n74283_1_pin14),
    .pin10(Input2[3]), .pin9(n74283_1_pin7), .pin8(n74283_1_pin12));
  _7404 #(.ShowInternalStructure("true")) u_7404_1 (
    .pin11(EN_SUB), .pin10(n74283_1_pin7), .pin9(EN_ADD), .pin8(n7404_1_pin8));  // open: pin1, pin2, pin3, pin4, pin5, pin6, pin13, pin12
  _7436 #(.ShowInternalStructure("true")) u_7436_1 (
    .pin1(n74283_1_pin7), .pin2(n7404_1_pin8), .pin3(n7436_1_pin3));  // open: pin4, pin5, pin6, pin13, pin12, pin11, pin10, pin9, pin8
  _74244 #(.ShowInternalStructure("true")) u_74244_5 (
    .pin1(n7436_1_pin3), .pin2(n74283_2_pin10), .pin3(out_4[3]), .pin4(n74283_2_pin13), .pin5(out_4[2]),
    .pin6(n74283_2_pin1), .pin7(out_4[1]), .pin8(n74283_2_pin4), .pin9(out_4[0]), .pin19(n7436_1_pin3),
    .pin18(out_4[7]), .pin17(n74283_1_pin10), .pin16(out_4[6]), .pin15(n74283_1_pin13), .pin14(out_4[5]),
    .pin13(n74283_1_pin1), .pin12(out_4[4]), .pin11(n74283_1_pin4));
  // also tied to GND on the sheet: n74138_1_pin4
  // also tied to VCC on the sheet: n74138_1_pin6

  // Other names for the same wires on the sheet: Result[7:0] = out_4
endmodule

module singleNumberCond (
  input  [2:0] Condition,
  input  [7:0] Number,
  output Result
);

  wire always_on, bigger_0, bigger_eq_0, eq_0, n7404_1_pin1, n7404_1_pin2, n7404_1_pin4, n7404_1_pin6,
       n7404_1_pin12, n7432_1_pin2, n7432_1_pin3, n7432_1_pin11, n7432_1_pin12, n7432_2_pin4, n7432_2_pin5,
       n7432_2_pin6, n7432_3_pin8, n7432_3_pin11, n74138_1_pin4, n74138_1_pin6, never, not_0, smaller_0,
       smaller_eq_0;

  _7432 #(.ShowInternalStructure("true")) u_7432_1 (
    .pin1(Number[5]), .pin2(n7432_1_pin2), .pin3(n7432_1_pin3), .pin4(Number[3]), .pin5(Number[4]),
    .pin6(n7432_1_pin2), .pin13(Number[2]), .pin12(n7432_1_pin12), .pin11(n7432_1_pin11), .pin10(Number[1]),
    .pin9(Number[0]), .pin8(n7432_1_pin12));
  _7432 #(.ShowInternalStructure("true")) u_7432_2 (
    .pin4(n7432_2_pin4), .pin5(n7432_2_pin5), .pin6(n7432_2_pin6), .pin13(Number[7]), .pin12(Number[6]),
    .pin11(n7432_2_pin4), .pin10(n7432_1_pin3), .pin9(n7432_1_pin11), .pin8(n7432_2_pin5));  // open: pin1, pin2, pin3
  _74138 #(.ShowInternalStructure("true"), .VccGndPorts("true")) u_74138_1 (
    .pin1(Condition[0]), .pin2(Condition[1]), .pin3(Condition[2]), .pin4(n74138_1_pin4),
    .pin5(n74138_1_pin4), .pin6(n74138_1_pin6), .pin7(bigger_0), .pin8(n74138_1_pin4), .pin16(n74138_1_pin6),
    .pin15(never), .pin14(eq_0), .pin13(smaller_0), .pin12(smaller_eq_0), .pin11(always_on), .pin10(not_0),
    .pin9(bigger_eq_0));
  _7404 #(.ShowInternalStructure("true")) u_7404_1 (
    .pin1(n7404_1_pin1), .pin2(n7404_1_pin2), .pin3(Number[7]), .pin4(n7404_1_pin4), .pin5(always_on),
    .pin6(n7404_1_pin6), .pin13(n7432_2_pin6), .pin12(n7404_1_pin12));  // open: pin11, pin10, pin9, pin8
  _7432 #(.ShowInternalStructure("true")) u_7432_3 (
    .pin1(Number[7]), .pin2(n7404_1_pin12), .pin3(n7404_1_pin1), .pin13(Number[7]), .pin12(n7404_1_pin12),
    .pin11(n7432_3_pin11), .pin10(n7404_1_pin4), .pin9(n7404_1_pin12), .pin8(n7432_3_pin8));  // open: pin4, pin5, pin6
  _74125 #(.ShowInternalStructure("true")) u_74125_1 (
    .pin1(bigger_0), .pin2(n7404_1_pin2), .pin3(Result), .pin4(smaller_0), .pin5(Number[7]), .pin6(Result),
    .pin13(always_on), .pin12(n7404_1_pin6), .pin11(Result));  // open: pin10, pin9, pin8
  _74125 #(.ShowInternalStructure("true")) u_74125_2 (
    .pin1(not_0), .pin2(n7432_2_pin6), .pin3(Result), .pin4(eq_0), .pin5(n7404_1_pin12), .pin6(Result),
    .pin13(smaller_eq_0), .pin12(n7432_3_pin11), .pin11(Result), .pin10(bigger_eq_0), .pin9(n7432_3_pin8),
    .pin8(Result));
  // also tied to GND on the sheet: n74138_1_pin4
  // also tied to VCC on the sheet: n74138_1_pin6
endmodule
